# Fritzing sketch boat (saved by Fritzing 0.9.3b)

parts:
  Arduino_Nano = Arduino Nano (Rev3.0)
  M1 = DC Motor
  M2 = DC Motor
  J1 = Infrared Proximity Sensor [part_number="Proximity sensor"]
  IC1 = L293D [package=THT]
  Part1 = Triple Axis Magnetometer - HMC5883 Breakout [part_number=Compass]
  VCC2 = Battery block 9V

nets:
  GND: Arduino_Nano.GND, J1.GND, IC1.0V, Part1.GND, VCC2.-
  N1: Arduino_Nano.D2, IC1.In_3
  N2: Arduino_Nano.D3, IC1.In_4
  N3: Arduino_Nano.D4, IC1.In_2
  N4: Arduino_Nano.D5, IC1.Enable_2
  N5: Arduino_Nano.D6, IC1.Enable_1
  N6: Arduino_Nano.D7, IC1.In_1
  N7: Arduino_Nano.VIN, IC1.+Vmotor, VCC2.+
  VCC: Arduino_Nano.5V, J1.Vcc, IC1.+V, Part1.VCC
  N8: Arduino_Nano.A5, Part1.SCL
  N9: Arduino_Nano.A4, Part1.SDA
  N10: Arduino_Nano.A0, J1.Vout
  N11: M1.pin_1, IC1.Out_1_(_Controlled_by_Enable_1_)
  N12: M1.pin_2, IC1.Out_2_(_Controlled_by_Enable_1_)
  N13: M2.pin_1, IC1.Out_4_(_Controlled_by_Enable_2_)
  N14: M2.pin_2, IC1.Out_3_(_Controlled_by_Enable_2_)
